# Fritzing sketch House_01 (saved by Fritzing 0.9.2b)
circuit board: 8.46667cm x 5.64444cm
breadboards: 1

parts:
  IR1 = TSOP312.., 314.. [package=THT]
  U4 = ESP8266 WiFi Module [part_number=ESP8266]
  Part5 = Arduino Uno (Rev3)
  DHT1 = DHT11 Humitidy and Temperature Sensor
  Adafruit_Bluefruit_HID1 = Adafruit Bluefruit Bluetooth Module  # not connected

nets:
  GND: IR1.GND, U4.GND, Part5.GND, DHT1.GND
  VCC: IR1.Vs, U4.VCC, Part5.D7, Part5.3V3, DHT1.VDD
  N1: Part5.D2, DHT1.DATA

notes:
  DHT 11
  Temperature / Humidity Sensor
  Arfuino Uno
  TSOP31238
  IR receiver
  ESP 8266
  WiFi
  KEDSUM
  Bluetooth
  Light Sensor

custom parts:
  ESP8266 WiFi Module: Generic WiFi Module based on the ESP8266 with onboard PCB antenna and UART communications
  DHT11 Humitidy and Temperature Sensor: DHT11 Humidity and Temperature Sensor
