# Fritzing sketch Led_01 (saved by Fritzing 0.9.2b)
circuit board: 7.6106cm x 5.45629cm
breadboards: 1

parts:
  Part1 = Arduino Uno (Rev3)
  FET1 = STP16NF06 N-Channel Power MOSFET
  FET2 = STP16NF06 N-Channel Power MOSFET
  FET3 = STP16NF06 N-Channel Power MOSFET
  Power_plug1 = Power plug
  R3 = Resistor [tolerance=±5% resistance=220 package="2512 [SMD]"]
  R1 = Resistor [tolerance=±5% resistance=220 package="2512 [SMD]"]
  R2 = Resistor [tolerance=±5% resistance=220 package="2512 [SMD]"]

nets:
  GND: Part1.GND, FET1.source, FET2.source, FET3.source, Power_plug1.GND, R3.Pin_0, R1.Pin_0, R2.Pin_0
  N1: Part1.D3_PWM, FET3.gate, R3.Pin_1
  N2: Part1.D5_PWM, FET2.gate, R2.Pin_1
  N3: Part1.D6_PWM, FET1.gate, R1.Pin_1

notes:
  12 V LED Power Supply
  LED Wiring connector

custom parts:
  STP16NF06 N-Channel Power MOSFET: STP16NF06 N-channel Power MOSFET

// code stored in the sketch: Home_Base_01.ino
/*
 * Home_Base project 01
 *
 * Arduino Uno
 * 
 *This is a base line project 
 */

#include<stdlib.h>
#include <SoftwareSerial.h>
#include <OneWire.h>
#include <DallasTemperature.h>		// DHT 11 - Temperature / Humidity sensor
#define ONE_WIRE_BUS 8
OneWire oneWire(ONE_WIRE_BUS);
DallasTemperature sensors(&oneWire);





void setup() {
    monitor.begin(9600);
    Serial.begin(9600);
    Serial.println("Home_01 - TEST PROGRAM ");
    Serial.println();
    sensor_setup();
    wifi_setup();
}

void loop() {
    sensor_loop();
    wifi_loop();
}

// ### END DBK
