# Fritzing sketch LPD003 (saved by Fritzing 0.9.1b)
circuit board: 4.5cm x 5.7cm
breadboards: 1

parts:
  U1 = OPA 2340 Dual Op-Amp [part_number=OPA2340 package="DIP8 [THT]"]
  U2 = OPA 2340 Dual Op-Amp [part_number="OPA 2340" package="DIP8 [THT]"]
  J1 = female pin header, 2 pins [form="♀ (female)"]
  R1 = Resistor [tolerance=±5% resistance=1M part_number=R1 package=THT]
  J2 = female pin header, 3 pins [form="♀ (female)"]
  R2 = Resistor [tolerance=±5% resistance=10k part_number=R2 package=THT]
  R3 = Resistor [tolerance=±5% resistance=1M part_number=R2 package=THT]
  R4 = Resistor [tolerance=±5% resistance=1M part_number=R2 package=THT]
  R5 = Resistor [tolerance=±5% resistance=1M part_number=R2 package=THT]
  R6 = Resistor [tolerance=±5% resistance=100k part_number=R2 package=THT]
  C2 = Ceramic Capacitor [capacitance=100nF package="200 mil [THT, multilayer]"]
  C1 = Ceramic Capacitor [capacitance=100nF package="200 mil [THT, multilayer]"]
  C3 = Ceramic Capacitor [capacitance=100nF package="200 mil [THT, multilayer]"]
  U3 = Voltage Regulator [package="TO220 [THT]"]
  J3 = mystery part, 3 pins [chip_label="Select Vcc"]
  part = Ceramic Capacitor [capacitance=100nF package="200 mil [THT, multilayer]"]  # not connected

nets:
  N1: U1.connector0, R1.Pin_0, J2.pin3, R4.Pin_0
  N2: U1.connector1, J1.pin2, R1.Pin_1, R2.Pin_1
  N3: U1.connector2, U2.connector0, U2.connector1, J1.pin1, R3.Pin_1, C2.0
  GND: U1.connector3, U2.connector3, J2.pin2, R6.Pin_0, C3.0, U3.Pin_1
  N4: U1.connector4, R4.Pin_1, C2.1
  N5: U1.connector5, R3.Pin_0, C1.1
  N6: U1.connector6, R2.Pin_0, C1.0
  3.3V: U1.connector7, U2.connector7, R5.Pin_1, C3.1, J3.pin2
  N7: U2.connector2, U2.connector4, R5.Pin_0, R6.Pin_1
  N8: U2.connector5, U2.connector6
  N9: J2.pin1, U3.Pin_3, J3.pin1
  N10: U3.Pin_2, J3.pin3

notes:
  K (-)
  A (+)
  BPW21
  +
  -
  P
  Rev. 1.0
  kWh meter, Lightpulse detector with daylight compensation, 1.0
  +3.3 V
  Gnd
  Puls out
  Oranje =Vref
  Pulse out
  +3.3V or 5V
  R1
  R2
  C1
  R3
  C2
  R4
  R5
  R6
  C3
  Geel =Pulse Out
  A
  K
  1
  2
  3
  ld1117
  v33

custom parts:
  OPA 2340 Dual Op-Amp: Single-Supply, Rail-to-Rail Operational Amplifiers
