# Fritzing sketch Arduino_SoundRange_01 (saved by Fritzing 0.9.2b)
circuit board: 8.46667cm x 5.64444cm
breadboards: 1

parts:
  Part1 = Arduino Uno (Rev3)
  Part2 = HC-SR04 Ultrasonic Rangemeter

nets:
  N1: Part1.D11_PWM/MOSI, Part2.Echo
  N2: Part1.D12/MISO, Part2.Trig
  GND: Part1.GND, Part2.GND
  5V: Part1.5V, Part2.VCC

notes:
  This is a 5 volt part !
