# Fritzing sketch Temperature_01 (saved by Fritzing 0.9.2b)
breadboards: 1

parts:
  Part1 = Arduino Uno (Rev3)
  DHT1 = DHT11 Humitidy and Temperature Sensor

nets:
  N1: Part1.D3_PWM, DHT1.DATA
  3V3: Part1.3V3, DHT1.VDD
  GND: Part1.GND, DHT1.GND

notes:
  DHT-11
  Temperature / Humidity
  Sensor
  The part I have is mounted on a small board with 3 pins
  The pinout is different - Beware!

custom parts:
  DHT11 Humitidy and Temperature Sensor: DHT11 Humidity and Temperature Sensor

// code stored in the sketch: Untitled.ino
/*
 * Home arduino package 01
 *
 * Arduino Uno
 * DHT11 Temperature Humidity Sensor
 *
 */

// Arduino
#include<stdlib.h>
#include <SoftwareSerial.h>
#include <OneWire.h>

// DHT 11 - Temperature / Humidity Sensor
#include <DallasTemperature.h>		// DHT 11 - Temperature / Humidity sensor
#define ONE_WIRE_BUS 8
OneWire oneWire(ONE_WIRE_BUS);
DallasTemperature sensors(&oneWire);
#define DHT11_PIN 2


// Utility 
void sendDebug(String cmd){
    monitor.print("SEND: ");
    monitor.println(cmd);
    Serial.println(cmd);
} 


// Temp Utils
void ReadTemp_loop(){
    sensors.requestTemperatures();
    float tempC = sensors.getTempCByIndex(0);
    tempC = DallasTemperature::toFahrenheit(tempC);
    char buffer[10];
    String tempF = dtostrf(tempC, 4, 1, buffer);
    updateTemp(tempF);
    delay(60000);
}

void updateTemp(String tenmpF){
    String cmd = "AT+CIPSTART=\"TCP\",\"";
    cmd += DST_IP;
    cmd += "\",80";
    sendDebug(cmd);
    delay(2000);
    if(Serial.find("Error")){
        monitor.print("RECEIVED: Error");
        return;
    }
    cmd = GET;
  cmd += tenmpF;
  cmd += "\r\n";
  Serial.print("AT+CIPSEND=");
  Serial.println(cmd.length());
  if(Serial.find(">")){
    monitor.print(">");
    monitor.print(cmd);
    Serial.print(cmd);
  }else{
    sendDebug("AT+CIPCLOSE");
  }
  if(Serial.find("OK")){
    monitor.println("RECEIVED: OK");
  }else{
    monitor.println("RECEIVED: Error");
  }
}


void sensor_setup() {
    sensors.begin();
}

void sensor_loop() {
    Serial.println("\n");
    int chk = sensors.getTempCByIndex(0);
    Serial.print("Read sensor: ");
    delay(2000);
}






void setup() {
    monitor.begin(9600);
    Serial.begin(9600);
    Serial.println("DHT11 - TEST PROGRAM ");
    Serial.println();
    sensor_setup();
}

void loop() {
    sensor_loop();
}

// ### END DBK
