# Fritzing sketch WiFi_01 (saved by Fritzing 0.9.2b)
breadboards: 1

parts:
  U1 = ESP8266 WiFi Module [part_number=ESP8266]
  Part1 = Arduino Uno (Rev3)

nets:
  N1: U1.RXD, Part1.D7
  VCC: U1.VCC, U1.CH_PD, Part1.3V3
  GND: U1.GND, Part1.GND
  N2: U1.TXD, Part1.D5_PWM

notes:
  ESP8266
  WiFi Module
  3.3v

custom parts:
  ESP8266 WiFi Module: Generic WiFi Module based on the ESP8266 with onboard PCB antenna and UART communications

// code stored in the sketch: ESP8266.ino
#define LUA_USE_BUILTIN_STRING    // for string.xxx()
#define LUA_USE_BUILTIN_TABLE   // for table.xxx()
#define LUA_USE_BUILTIN_COROUTINE // for coroutine.xxx()
#define LUA_USE_BUILTIN_MATH    // for math.xxx(), partially work
// #define LUA_USE_BUILTIN_IO       // for io.xxx(), partially work

// #define LUA_USE_BUILTIN_OS     // for os.xxx(), not work
// #define LUA_USE_BUILTIN_DEBUG    // for debug.xxx(), not work

#define LUA_USE_MODULES

#ifdef LUA_USE_MODULES
#define LUA_USE_MODULES_NODE
#define LUA_USE_MODULES_FILE
#define LUA_USE_MODULES_GPIO
#define LUA_USE_MODULES_WIFI
#define LUA_USE_MODULES_NET
#define LUA_USE_MODULES_PWM
#define LUA_USE_MODULES_I2C
#define LUA_USE_MODULES_SPI
#define LUA_USE_MODULES_TMR
#define LUA_USE_MODULES_ADC
#define LUA_USE_MODULES_UART
#define LUA_USE_MODULES_OW
#define LUA_USE_MODULES_BIT
#define LUA_USE_MODULES_MQTT
// #define LUA_USE_MODULES_COAP
#define LUA_USE_MODULES_U8G
#define LUA_USE_MODULES_WS2812
#define LUA_USE_MODULES_CJSON
#endif /* LUA_USE_MODULES */


    ip = wifi.sta.getip()
    print(ip)
    //--nil
    wifi.setmode(wifi.STATION)
    wifi.sta.config("SSID","password")
    ip = wifi.sta.getip()
    print(ip)
    //--192.168.18.110



    pin = 1
    gpio.mode(pin,gpio.OUTPUT)
    gpio.write(pin,gpio.HIGH)
    print(gpio.read(pin))


    //-- A simple http client
    conn=net.createConnection(net.TCP, 0);
    conn:on("receive", function(conn, payload) print(payload) end );
    conn:connect(80,"115.239.210.27");
    conn:send("GET / HTTP/1.1\r\nHost: www.baidu.com\r\nConnection: keep-alive\r\nAccept: */*\r\n\r\n");



    //-- A simple http server
    srv=net.createServer(net.TCP)
    srv:listen(80,function(conn)
      conn:on("receive",function(conn,payload)
        print(payload)
        conn:send("<h1> Hello, NodeMcu.</h1>")
      end)
      conn:on("sent",function(conn) conn:close() end)
    end)



-- init mqtt client with keepalive timer 120sec
m = mqtt.Client("clientid", 120, "user", "password")

-- setup Last Will and Testament (optional)
-- Broker will publish a message with qos = 0, retain = 0, data = "offline"
-- to topic "/lwt" if client don't send keepalive packet
m:lwt("/lwt", "offline", 0, 0)

m:on("connect", function(con) print ("connected") end)
m:on("offline", function(con) print ("offline") end)

-- on publish message receive event
m:on("message", function(conn, topic, data)
  print(topic .. ":" )
  if data ~= nil then
    print(data)
  end
end)

-- for secure: m:connect("192.168.11.118", 1880, 1)
m:connect("192.168.11.118", 1880, 0, function(conn) print("connected") end)

-- subscribe topic with qos = 0
m:subscribe("/topic",0, function(conn) print("subscribe success") end)
-- or subscribe multiple topic (topic/0, qos = 0; topic/1, qos = 1; topic2 , qos = 2)
-- m:subscribe({["topic/0"]=0,["topic/1"]=1,topic2=2}, function(conn) print("subscribe success") end)
-- publish a message with data = hello, QoS = 0, retain = 0
m:publish("/topic","hello",0,0, function(conn) print("sent") end)

m:close();
-- you can call m:connect again




-- a udp server
s=net.createServer(net.UDP)
s:on("receive",function(s,c) print(c) end)
s:listen(5683)

-- a udp client
cu=net.createConnection(net.UDP)
cu:on("receive",function(cu,c) print(c) end)
cu:connect(5683,"192.168.18.101")
cu:send("hello")


  function led(r,g,b)
    pwm.setduty(1,r)
    pwm.setduty(2,g)
    pwm.setduty(3,b)
  end
  pwm.setup(1,500,512)
  pwm.setup(2,500,512)
  pwm.setup(3,500,512)
  pwm.start(1)
  pwm.start(2)
  pwm.start(3)
  led(512,0,0) -- red
  led(0,0,512) -- blue



  lighton=0
  tmr.alarm(1,1000,1,function()
    if lighton==0 then
      lighton=1
      led(512,512,512)
    else
      lighton=0
      led(0,0,0)
    end
  end)



  --init.lua will be excuted
  file.open("init.lua","w")
  file.writeline([[print("Hello, do this at the beginning.")]])
  file.close()
  node.restart()  -- this will restart the module.



    -- a simple telnet server
    s=net.createServer(net.TCP,180)
    s:listen(2323,function(c)
       function s_output(str)
          if(c~=nil)
             then c:send(str)
          end
       end
       node.output(s_output, 0)   -- re-direct output to function s_ouput.
       c:on("receive",function(c,l)
          node.input(l)           -- works like pcall(loadstring(l)) but support multiple separate line
       end)
       c:on("disconnection",function(c)
          node.output(nil)        -- un-regist the redirect output function, output goes to serial
       end)
       print("Welcome to NodeMcu world.")
    end)



    -- read temperature with DS18B20
    node.compile("ds18b20.lua")   --  run this only once to compile and save to "ds18b20.lc"
    t=require("ds18b20")
    t.setup(9)
    addrs=t.addrs()
    -- Total DS18B20 numbers, assume it is 2
    print(table.getn(addrs))
    -- The first DS18B20
    print(t.read(addrs[1],t.C))
    print(t.read(addrs[1],t.F))
    print(t.read(addrs[1],t.K))
    -- The second DS18B20
    print(t.read(addrs[2],t.C))
    print(t.read(addrs[2],t.F))
    print(t.read(addrs[2],t.K))
    -- Just read
    print(t.read())
    -- Just read as centigrade
    print(t.read(nil,t.C))
    -- Don't forget to release it after use
    t = nil
    ds18b20 = nil
    package.loaded["ds18b20"]=nil

// code stored in the sketch: WiFi_01.ino
/*
 * WiFi_01
 *
 * Arduino Uno
 * 
 *This is a base line project 
 */
 #include<stdlib.h>
#include <SoftwareSerial.h>
SoftwareSerial monitor(5, 7); // RX, TX


// Include various modules here
// Module WiFi_01 - Connect to WiFi access point
#include <ESP8266.h>    // C:\Users\briank\Downloads\Projects\libraries\ITEADLIB_Arduino_WeeESP8266-master (legacy)
// Pins
#define WIFI_TX  7
#define WIFI_RX  5
#define WIFI_SSID        "SID_NAME"
#define WIFI_PASSWORD    "123456789"
ESP8266 wifi(monitor);    // Instantiate
void print_bool(char* p_name, bool p_value) {
    Serial.print(p_name);
    if (p_value) Serial.println(" Success.");
    else Serial.println(" Failure.");
}
void wifiRestart() {
    bool l_erc = wifi.restart();
    print_bool("Restart: ", l_erc);
}
void wifiKick() {
    bool l_erc = wifi.kick();
    print_bool("Kick: ", l_erc);
}
void wifiGetVersion() {
    String l_version = wifi.getVersion().c_str();
    Serial.print("Firmware Version: ");
    Serial.println(l_version);
}
void wifiOprToStation() {
    bool l_erc = wifi.setOprToStation();
    print_bool("Set Operation Mode to Station: ", l_erc);
}
void wifiOprToSoftAP() {
    bool l_erc = wifi.setOprToSoftAP();
    print_bool("Set Operation Mode to SoftAP: ", l_erc);
}
void wifiOprToStationSoftAP() {
    bool l_erc = wifi.setOprToStationSoftAP();
    print_bool("Set Operation Mode to StationSoftAP: ", l_erc);
}
void wifiJoinAP(String p_ssid, String p_password) {
    bool l_erc = wifi.joinAP(WIFI_SSID, WIFI_PASSWORD);
    print_bool("Join AP: ", l_erc);
}
void wifiListAPs() {
    String l_ret = wifi.getAPList();
    Serial.println("List of APs: ");
    Serial.println(l_ret);
    Serial.println("__________");
}
void wifi_setup() {
    Serial.print("wifi_setup begin\n");
    wifiRestart();
    wifiKick();
    wifiGetVersion();
    wifiOprToStation();
    wifiOprToSoftAP();
    wifiOprToStationSoftAP();
    wifiJoinAP(WIFI_SSID, WIFI_PASSWORD);
    wifiListAPs();
    // Serial.print("setup end\r\n");
}
void wifi_loop() {
}
// Module END - WiFi



// Standard setup and loop
void setup() {
    monitor.begin(9600);
    Serial.begin(9600);
    Serial.println("WiFi_01\n");
    // Include vaarious module setups here.
    wifi_setup();
}
void loop() {
    // Include various module loops here.
    wifi_loop();
}

// ### END DBK
